# Fritzing sketch CO_potable_Sensor (saved by Fritzing 1.0.8)
breadboards: 1

parts:
  Part1 = Power Cell LiPo Charger/Booster
  Adafruit_bq25185_with_5V_Boost_Breakout1 = Adafruit bq25185 with 5V Boost Breakout [part_number=#6106]
  S1 = SWITCH-DPDT [package=gpi-152-3013]
  VR1 = LM2577 (TO263) [part_number=LM2577 package=TO263]
  Part2 = Gas Sensor Breakout Board
  R1 = Resistor [tolerance=±5% power=0.25W resistance=1k package=THT]
  R2 = Resistor [tolerance=±5% power=0.25W resistance=2000 package=THT]
  Adafruit_USB_Host_BFF1 = Adafruit USB Host BFF [mn=Adafruit mpn=#5956 part_number=#5956]
  Part3 = OLED Color 1.5 inch 128x128 w microSD [part_number=1431]
  J1 = Piezo Speaker

nets:
  N1: Part1.5VIN, Adafruit_bq25185_with_5V_Boost_Breakout1.VBAT
  GND: Part1.GND, Adafruit_bq25185_with_5V_Boost_Breakout1.GND, VR1.COMP
  N2: Adafruit_bq25185_with_5V_Boost_Breakout1.+5V, S1.6
  N3: S1.5, VR1.GND
  GND_2: VR1.FB, Part2.GND, R1.Pin_0, R1.Pin_1, R2.Pin_1, Adafruit_USB_Host_BFF1.IRQ, Adafruit_USB_Host_BFF1.GND, Part3.GND, J1.pin1
  N4: VR1.SW, Adafruit_USB_Host_BFF1.+5V
  N5: VR1.VIN, Part2.B1
  N6: Part2.A1, R2.Pin_0
  N7: Adafruit_USB_Host_BFF1.SDA, Part3.SD_MISO
  N8: Adafruit_USB_Host_BFF1.SCL, Part3.SD_CS
  3.3V: Adafruit_USB_Host_BFF1.3.3V, Part3.3.3V

notes:
  Some parts where replace due to their absence in fritzing to build the final demo assembly.
